# Fritzing sketch rele2 (saved by Fritzing 0.9.3b)
breadboards: 1

parts:
  S1 = Pushbutton [package="[THT]"]
  F1 = FUSE [package=fuse_5mm]
  U1 = RELAY-2 [package=relay-g5v]
  5V = DC-DC_CONVERTER [package=dc-dc_converter]
  D1 = Rectifier Diode [part_number=1N4007 package="300 mil [THT]"]
  D2 = Rectifier Diode [part_number=1N4007 package="300 mil [THT]"]
  Raspberry_Pi_1 = Raspberry Pi 3 [part_number=RPI-3-V1.2]
  C1 = Ceramic Capacitor [capacitance=10nF package="0603 [SMD, multilayer]"]
  Q1 = TRANSISTOR_PNP [part_number=SS8550 package=to-92]
  R6 = Resistor [tolerance=±5% resistance=47k package="2010 [SMD]"]
  D6 = Rectifier Diode [part_number=1N4007 package="300 mil [THT]"]
  Q2 = TRANSISTOR_PNP [part_number=SS8550 package=to-92]
  R7 = Resistor [tolerance=±5% resistance=10k package=THT]
  J1 = Screw terminal - 2 pins [package=THT]
  R11 = Resistor [tolerance=±5% resistance=220 package="2010 [SMD]"]
  LED1 = LED - 5mm [color="Red (633nm)" package="5 mm [THT]"]
  C2 = Electrolytic Capacitor [capacitance=100nF package="0605 [SMD, electrolytic]"]
  D7 = Zener Diode [part_number=1N4732A breakdown_voltage=5.1V package="Melf DO-213 AB [SMD]"]
  R12 = Resistor [tolerance=±5% resistance=1.5k package=THT]
  U2 = TRIAC [package=to-92]
  C3 = Electrolytic Capacitor [capacitance=10μF package="0605 [SMD, electrolytic]"]
  U7 = Voltage Regulator - 5V [package="DPak [SMD]"]
  5V1 = DC-DC_CONVERTER [package=dc-dc_converter]
  S2 = Pushbutton [package="[THT]"]
  F2 = FUSE [package=fuse_5mm]
  C4 = Ceramic Capacitor [capacitance=10nF package="0603 [SMD, multilayer]"]
  J2 = Screw terminal - 2 pins [package=THT]
  U8 = RELAY-2 [package=relay-g5v]
  D8 = Rectifier Diode [part_number=1N4007 package="300 mil [THT]"]
  Q3 = TRANSISTOR_PNP [part_number=SS8550 package=to-92]
  R13 = Resistor [tolerance=±5% resistance=47k package="2010 [SMD]"]
  Q4 = TRANSISTOR_PNP [part_number=SS8550 package=to-92]
  D9 = Rectifier Diode [part_number=1N4007 package="300 mil [THT]"]
  R14 = Resistor [tolerance=±5% resistance=10k package=THT]
  U9 = Voltage Regulator - 5V [package="DPak [SMD]"]
  U10 = TLP621 [package=THT]
  C5 = Electrolytic Capacitor [capacitance=100nF package="0605 [SMD, electrolytic]"]  # not connected
  Raspberry_Pi_2 = Raspberry Pi 3 [part_number=RPI-3-V1.2]
  C6 = Ceramic Capacitor [capacitance=100nF package="100 mil [THT, multilayer]"]
  C7 = Ceramic Capacitor [capacitance=330nF package="100 mil [THT, multilayer]"]

nets:
  N1: S1.Pin_1, S1.Pin_2, C1.0, U7.input_voltage, C7.1
  N2: S1.Pin_3, S1.Pin_4, F1.2, U1.5, C1.1
  N3: F1.1, J1.pin1
  GND: U1.2, 5V.GND1, D2.anode, Raspberry_Pi_1.GND, R7.Pin_0, J1.pin2, LED1.cathode, C2.-, R12.Pin_0, U2.M1, C3.-, U7.GND, J2.pin2, U8.5, U8.9, D8.anode, R14.Pin_0, U9.GND, U10.Pin_2, U10.Pin_3, Raspberry_Pi_2.GND, C6.1, C7.0
  N4: U1.9, D1.cathode, D2.cathode, D6.cathode
  N5: U1.10, 5V.VIN
  5V: 5V.VOUT, Raspberry_Pi_1.3v3, Raspberry_Pi_1.3V3, Q1.E, R11.Pin_1, C2.+, D7.cathode, U2.M2, 5V1.VOUT, Q3.E, Raspberry_Pi_2.5V
  N6: D1.anode, Raspberry_Pi_1.GIPO19, U7.output_voltage, C6.0
  N7: Raspberry_Pi_1.GIPO26, Q2.B
  N8: Q1.B, R6.Pin_0
  N9: Q1.C, D6.anode
  N10: R6.Pin_1, Q2.E
  N11: Q2.C, R7.Pin_1
  N12: R11.Pin_0, LED1.anode
  N13: D7.anode, R12.Pin_1, U2.G, C3.+
  N14: 5V1.VIN, S2.Pin_3, S2.Pin_4, F2.2, C4.1
  N15: 5V1.GND1, U8.10
  N16: S2.Pin_1, S2.Pin_2, C4.0, U9.input_voltage
  N17: F2.1, J2.pin1
  N18: U8.2, D8.cathode, D9.cathode, U9.output_voltage, U10.Pin_1
  N19: Q3.B, R13.Pin_0
  N20: Q3.C, D9.anode
  N21: R13.Pin_1, Q4.E
  N22: Q4.B, Raspberry_Pi_2.GIPO26
  N23: Q4.C, R14.Pin_1
  N24: U10.Pin_4, Raspberry_Pi_2.GIPO19
